// Logisim project hyperCast.circ as structural Verilog: 33 circuits, main circuit main
module Memory (
  input  NeedSomething,
  input  [31:0] VALUE,
  input  [31:0] ADDRESS,
  input  Store,
  input  CLOCK,
  input  Cache_ativo,
  output ClockFake,
  output [31:0] out_8
);

  wire and_1_out, cache_1_isvalidcache, multiplexer_2_out, not_1_out, not_2_out, or_1_out,
       repetidoratraso_1_clockout;
  wire [15:0] short_32_16_1_out_2;
  wire [31:0] cache_1_cacheinstruction, controlled_buffer_1_out, VALID_BIT_data;

  assign controlled_buffer_1_out = Store ? VALUE : 32'bz;  // Controlled_Buffer controlled_buffer_1
  short_32_16 short_32_16_1 (.in_1(ADDRESS), .out_2(short_32_16_1_out_2));
  not not_1 (not_1_out, Store);
  CACHE cache_1 (
    .posicao(short_32_16_1_out_2), .toSave(Store), .clock(CLOCK), .isValidCache(cache_1_isvalidcache),
    .CacheInstruction(cache_1_cacheinstruction), .dados(controlled_buffer_1_out), .ValidBit(1'b1));
  RAM #(.addrWidth(16), .dataWidth(32), .bus("separate"), .Select("high"), .simpleMode("false")) VALID_BIT (
    .addr(short_32_16_1_out_2), .din(controlled_buffer_1_out), .data(VALID_BIT_data), .str(Store),
    .clk(CLOCK), .ld(not_1_out));  // open: sel, clr
  RepetidorAtraso repetidoratraso_1 (.clock(CLOCK), .clockOut(repetidoratraso_1_clockout), .GoodToGo(NeedSomething));
  and and_1 (and_1_out, cache_1_isvalidcache, Cache_ativo);
  not not_2 (not_2_out, NeedSomething);
  or or_1 (or_1_out, repetidoratraso_1_clockout, and_1_out, not_2_out);
  Multiplexer #(.width(32), .enable("false")) multiplexer_1 (
    .in0(VALID_BIT_data), .in1(cache_1_cacheinstruction), .out(out_8), .sel(and_1_out));
  Multiplexer #(.enable("false")) multiplexer_2 (.in0(or_1_out), .in1(CLOCK), .out(multiplexer_2_out), .sel(and_1_out));
  and and_2 (ClockFake, multiplexer_2_out, CLOCK);
endmodule

module main (
  input  CACHE_ATIVO,
  input  RESET_INST,
  output [31:0] out_3,
  output [31:0] out_4,
  output [31:0] out_5,
  output [31:0] out_6,
  output [31:0] Memory_Address,
  output [31:0] out_8,
  output [31:0] out_9,
  output [31:0] out_10,
  output [31:0] Memory_Value,
  output [31:0] out_12,
  output [3:0] out_13,
  output [3:0] out_14,
  output [3:0] out_15,
  output [3:0] out_16,
  output [3:0] out_17,
  output [3:0] out_18,
  output [3:0] out_19,
  output [3:0] out_20,
  output [3:0] out_21,
  output [3:0] out_22
);

  wire and_1_out, and_2_out, clock_1_out, codereader_1_if_equal, codereader_1_if_not_equal,
       codereader_1_jump, codereader_1_li, codereader_1_lw, codereader_1_out_14, codereader_1_sw,
       counter_instruction_1_need_to_flush_memory, instruction_position_1_need_to_flush,
       is_aritimetic_1_is_aritimetic, isstopcommand_1_isstopprocess, memory_1_clockfake, multiplexer_1_out,
       not_1_out, not_2_out, not_3_out, or_1_out, or_2_out, or_3_out, pipeline_1_1_if_equal_2,
       pipeline_1_1_if_less_or_equal_2, pipeline_1_1_is_enabled, pipeline_1_1_jump_2,
       pipeline_1_1_kill_process_2, pipeline_1_1_li_2, pipeline_1_1_lw_2, pipeline_1_1_sw_2,
       pipeline_2_1_if_equal_2, pipeline_2_1_if_less_or_equal_2, pipeline_2_1_is_enabled,
       pipeline_2_1_jump_2, pipeline_2_1_li_2, pipeline_2_1_lw_2, pipeline_2_1_sw_2,
       pipeline_2_1_true_statement_2, pipeline_register_1_if_equal_2, pipeline_register_1_if_less_or_equal_2,
       pipeline_register_1_is_enabled, pipeline_register_1_jump_2, pipeline_register_1_li_2,
       pipeline_register_1_lw_2, pipeline_register_1_sw_2, save_in_register_1_to_save,
       ula_1_statement_is_true;
  wire [3:0] codereader_1_op_code, codereader_1_r1, codereader_1_r2, codereader_1_r3, pipeline_1_1_opcode_2,
       pipeline_1_1_rd_2, pipeline_1_1_rt2_2, pipeline_1_1_rt_2, pipeline_2_1_opcode_2, pipeline_2_1_ts_2,
       pipeline_register_1_opcode_2, pipeline_register_1_t1_2, pipeline_register_1_t2_2,
       pipeline_register_1_ts_2;
  wire [15:0] adder_1_out, counter_instruction_1_next_address, instruction_position_1_out_6, register_1_q;
  wire [31:0] codereader_1_imediatte_address, handle_errors_1_new_rt1, handle_errors_1_new_rt2,
       handle_errors_1_new_rt3, handle_errors_2_new_rt1, handle_errors_2_new_rt2, handle_errors_2_new_rt3,
       pipeline_1_1_integer_2, pipeline_2_1_integer_2, pipeline_2_1_rt_2, pipeline_register_1_integer_2,
       pipeline_register_1_rd_2, pipeline_register_1_rt2, pipeline_register_1_rt_3, ram_1_data,
       registradores_1_r1, registradores_1_r2, registradores_1_rd, save_in_register_1_out_8, ula_1_result;

  codeReader codereader_1 (
    .in_1(ram_1_data), .OP_CODE(codereader_1_op_code), .R1(codereader_1_r1), .R2(codereader_1_r2),
    .R3(codereader_1_r3), .IMEDIATTE_ADDRESS(codereader_1_imediatte_address), .LI(codereader_1_li),
    .SW(codereader_1_sw), .LW(codereader_1_lw), .JUMP(codereader_1_jump), .IF_EQUAL(codereader_1_if_equal),
    .IF_NOT_EQUAL(codereader_1_if_not_equal), .kill_everyone(instruction_position_1_need_to_flush),
    .out_14(codereader_1_out_14));
  Pipeline_1 pipeline_1_1 (
    .OPCODE(codereader_1_op_code), .RT(codereader_1_r1), .RT2(codereader_1_r2), .RD(codereader_1_r3),
    .LI(codereader_1_li), .SW(codereader_1_sw), .LW(codereader_1_lw), .JUMP(codereader_1_jump),
    .IF_EQUAL(codereader_1_if_equal), .IF_LESS_OR_EQUAL(codereader_1_if_not_equal),
    .CLOCK(multiplexer_1_out), .OPCODE_2(pipeline_1_1_opcode_2), .RT_2(pipeline_1_1_rt_2),
    .RT2_2(pipeline_1_1_rt2_2), .RD_2(pipeline_1_1_rd_2), .LI_2(pipeline_1_1_li_2), .SW_2(pipeline_1_1_sw_2),
    .LW_2(pipeline_1_1_lw_2), .JUMP_2(pipeline_1_1_jump_2), .IF_EQUAL_2(pipeline_1_1_if_equal_2),
    .IF_LESS_OR_EQUAL_2(pipeline_1_1_if_less_or_equal_2), .INTEGER(codereader_1_imediatte_address),
    .INTEGER_2(pipeline_1_1_integer_2), .IS_ENABLED(pipeline_1_1_is_enabled), .RESET(or_2_out),
    .KILL_PROCESS(codereader_1_out_14), .KILL_PROCESS_2(pipeline_1_1_kill_process_2));
  Registradores registradores_1 (
    .in_1(pipeline_1_1_rt_2), .in_2(pipeline_1_1_rt2_2), .R1(registradores_1_r1), .R2(registradores_1_r2),
    .in_5(save_in_register_1_out_8), .in_6(multiplexer_1_out), .in_7(pipeline_1_1_rd_2),
    .RD(registradores_1_rd), .TO_SAVE(save_in_register_1_to_save), .Register_Saver(pipeline_2_1_ts_2));
  and and_1 (and_1_out, memory_1_clockfake, pipeline_2_1_is_enabled);
  REGISTERS_OUTPUT registers_output_1 (
    .OPCODE(pipeline_1_1_opcode_2), .R1(registradores_1_r1), .R2(registradores_1_r2),
    .RD(registradores_1_rd), .T1(pipeline_1_1_rt_2), .T2(pipeline_1_1_rt2_2), .TS(pipeline_1_1_rd_2),
    .OPCODE_2(out_22), .R1_2(out_4), .R2_2(out_6), .RD_2(out_10), .T1_2(out_14), .T2_2(out_16), .TS_2(out_19));
  or or_1 (or_1_out, and_1_out, not_1_out);
  not not_1 (not_1_out, pipeline_2_1_is_enabled);
  HANDLE_ERRORS handle_errors_1 (
    .T1(pipeline_1_1_rt_2), .T2(pipeline_1_1_rt2_2), .TS_2(pipeline_1_1_rd_2), .RD(registradores_1_rd),
    .TS(pipeline_2_1_ts_2), .VALUE_FINAL_CODE(save_in_register_1_out_8), .NEW_RT1(handle_errors_1_new_rt1),
    .NEW_RT2(handle_errors_1_new_rt2), .NEW_RT3(handle_errors_1_new_rt3), .R1(registradores_1_r1),
    .R2(registradores_1_r2), .HAVE_FUTURE_SIGHT(pipeline_1_1_is_enabled),
    .NORMAL_OP(is_aritimetic_1_is_aritimetic), .LI(pipeline_2_1_li_2));
  or or_2 (or_2_out, RESET_INST, pipeline_1_1_kill_process_2);
  Multiplexer #(.enable("false")) multiplexer_1 (.in0(1'b0), .in1(and_2_out), .out(multiplexer_1_out), .sel(or_1_out));
  and and_2 (and_2_out, clock_1_out, or_3_out);
  Clock clock_1 (.out(clock_1_out));
  PIPELINE_REGISTER pipeline_register_1 (
    .RT(handle_errors_1_new_rt1), .RD(handle_errors_1_new_rt3), .LI(pipeline_1_1_li_2),
    .SW(pipeline_1_1_sw_2), .LW(pipeline_1_1_lw_2), .JUMP(pipeline_1_1_jump_2),
    .IF_EQUAL(pipeline_1_1_if_equal_2), .IF_LESS_OR_EQUAL(pipeline_1_1_if_less_or_equal_2),
    .INTEGER(pipeline_1_1_integer_2), .CLOCK(multiplexer_1_out), .RT_3(pipeline_register_1_rt_3),
    .RD_2(pipeline_register_1_rd_2), .LI_2(pipeline_register_1_li_2), .SW_2(pipeline_register_1_sw_2),
    .LW_2(pipeline_register_1_lw_2), .JUMP_2(pipeline_register_1_jump_2),
    .IF_EQUAL_2(pipeline_register_1_if_equal_2), .IF_LESS_OR_EQUAL_2(pipeline_register_1_if_less_or_equal_2),
    .INTEGER_2(pipeline_register_1_integer_2), .RT_2(handle_errors_1_new_rt2), .RT2(pipeline_register_1_rt2),
    .T1(pipeline_1_1_rt_2), .T1_2(pipeline_register_1_t1_2), .T2(pipeline_1_1_rt2_2),
    .T2_2(pipeline_register_1_t2_2), .OPCODE(pipeline_1_1_opcode_2), .OPCODE_2(pipeline_register_1_opcode_2),
    .RESET(or_2_out), .IS_ABLE(pipeline_1_1_is_enabled), .IS_ENABLED(pipeline_register_1_is_enabled),
    .TS(pipeline_1_1_rd_2), .TS_2(pipeline_register_1_ts_2));
  or or_3 (or_3_out, not_2_out, not_3_out);
  not not_2 (not_2_out, pipeline_2_1_is_enabled);
  HANDLE_ERRORS handle_errors_2 (
    .T1(pipeline_register_1_t1_2), .T2(pipeline_register_1_t2_2), .TS_2(pipeline_register_1_ts_2),
    .RD(pipeline_register_1_rd_2), .TS(pipeline_2_1_ts_2), .VALUE_FINAL_CODE(save_in_register_1_out_8),
    .NEW_RT1(handle_errors_2_new_rt1), .NEW_RT2(handle_errors_2_new_rt2), .NEW_RT3(handle_errors_2_new_rt3),
    .R1(pipeline_register_1_rt_3), .R2(pipeline_register_1_rt2), .HAVE_FUTURE_SIGHT(pipeline_2_1_is_enabled),
    .NORMAL_OP(is_aritimetic_1_is_aritimetic), .LI(pipeline_2_1_li_2));
  ULA ula_1 (
    .R1(handle_errors_2_new_rt1), .R2(handle_errors_2_new_rt2), .in_3(pipeline_register_1_opcode_2),
    .RESULT(ula_1_result), .STATEMENT_IS_TRUE(ula_1_statement_is_true), .RS(handle_errors_2_new_rt3));
  ULA_OUTPUT ula_output_1 (
    .OPCODE(pipeline_register_1_opcode_2), .R1(handle_errors_2_new_rt1), .R2(handle_errors_2_new_rt2),
    .RD(ula_1_result), .T1(pipeline_register_1_t1_2), .T2(pipeline_register_1_t2_2),
    .TS(pipeline_register_1_ts_2), .OPCODE_2(out_21), .R1_2(out_3), .R2_2(out_5), .RD_2(out_9),
    .T1_2(out_13), .T2_2(out_15), .TS_2(out_18));
  OUTPUT output_1 (
    .OPCODE(pipeline_2_1_opcode_2), .RD(save_in_register_1_out_8), .TS(pipeline_2_1_ts_2),
    .ADDRESS(pipeline_2_1_rt_2), .OPCODE_2(out_20), .RESULT(out_8), .IN_THIS_REGISTER(out_17),
    .ADDRESS_2(out_12));
  Pipeline_2 pipeline_2_1 (
    .TRUE_STATEMENT(ula_1_statement_is_true), .RT(handle_errors_2_new_rt1), .RD(ula_1_result),
    .LI(pipeline_register_1_li_2), .SW(pipeline_register_1_sw_2), .LW(pipeline_register_1_lw_2),
    .JUMP(pipeline_register_1_jump_2), .IF_EQUAL(pipeline_register_1_if_equal_2),
    .IF_LESS_OR_EQUAL(pipeline_register_1_if_less_or_equal_2), .CLOCK(multiplexer_1_out),
    .INTEGER(pipeline_register_1_integer_2), .TRUE_STATEMENT_2(pipeline_2_1_true_statement_2),
    .RT_2(pipeline_2_1_rt_2), .RD_2(Memory_Address), .LI_2(pipeline_2_1_li_2), .SW_2(pipeline_2_1_sw_2),
    .LW_2(pipeline_2_1_lw_2), .JUMP_2(pipeline_2_1_jump_2), .IF_EQUAL_2(pipeline_2_1_if_equal_2),
    .IF_LESS_OR_EQUAL_2(pipeline_2_1_if_less_or_equal_2), .INTEGER_2(pipeline_2_1_integer_2),
    .T1(pipeline_register_1_t1_2), .TS(pipeline_register_1_ts_2), .TS_2(pipeline_2_1_ts_2),
    .OPCODE(pipeline_register_1_opcode_2), .OPCODE_2(pipeline_2_1_opcode_2),
    .IS_ABLE(pipeline_register_1_is_enabled), .IS_ENABLED(pipeline_2_1_is_enabled), .RESET(or_2_out));  // open: T1_2
  COUNTER_INSTRUCTION counter_instruction_1 (
    .ADDRESS_CURRENT(instruction_position_1_out_6), .CONDITION_IS_TRUE(pipeline_2_1_true_statement_2),
    .STATE_TYPE_1(pipeline_2_1_if_less_or_equal_2), .STATE_TYPE_2(pipeline_2_1_if_equal_2),
    .ADDRESS_JUMP(Memory_Address), .WHANT_TO_JUMP(pipeline_2_1_jump_2), .IS_ACTIVE(pipeline_2_1_is_enabled),
    .NEED_TO_FLUSH_MEMORY(counter_instruction_1_need_to_flush_memory),
    .NEXT_ADDRESS(counter_instruction_1_next_address), .STOP_PROCESS(isstopcommand_1_isstopprocess));
  isStopCommand isstopcommand_1 (.OPCODE(pipeline_2_1_opcode_2), .isStopProcess(isstopcommand_1_isstopprocess));
  IS_ARITIMETIC is_aritimetic_1 (.in_1(pipeline_2_1_opcode_2), .IS_ARITIMETIC(is_aritimetic_1_is_aritimetic));
  instruction_position instruction_position_1 (
    .in_1(counter_instruction_1_next_address), .clock(multiplexer_1_out),
    .FLUSH_MEMORY(counter_instruction_1_need_to_flush_memory), .out_6(instruction_position_1_out_6),
    .NEED_TO_FLUSH(instruction_position_1_need_to_flush), .RESET(RESET_INST),
    .isStopProcess(isstopcommand_1_isstopprocess));
  Hex_Digit_Display hex_digit_display_1 (.value(register_1_q[15:12]));  // open: dp
  Hex_Digit_Display hex_digit_display_2 (.value(register_1_q[11:8]));  // open: dp
  Hex_Digit_Display hex_digit_display_3 (.value(register_1_q[7:4]));  // open: dp
  Memory memory_1 (
    .VALUE(Memory_Address), .ADDRESS(pipeline_2_1_rt_2), .Store(pipeline_2_1_sw_2), .CLOCK(and_2_out),
    .out_8(Memory_Value), .ClockFake(memory_1_clockfake), .NeedSomething(pipeline_2_1_lw_2),
    .Cache_ativo(CACHE_ATIVO));
  SAVE_IN_REGISTER save_in_register_1 (
    .LI(pipeline_2_1_li_2), .out_8(save_in_register_1_out_8), .IMMEDIATE(pipeline_2_1_integer_2),
    .FROM_MEMORY(Memory_Value), .FROM_ULA(Memory_Address), .LW(pipeline_2_1_lw_2),
    .TO_SAVE(save_in_register_1_to_save), .NORMAL_OP(is_aritimetic_1_is_aritimetic));
  Hex_Digit_Display hex_digit_display_4 (.value(register_1_q[3:0]));  // open: dp
  not not_3 (not_3_out, isstopcommand_1_isstopprocess);
  RAM #(.addrWidth(16), .dataWidth(32), .Select("high"), .simpleMode("false")) ram_1 (
    .addr(instruction_position_1_out_6), .data(ram_1_data), .sel(not_3_out));  // open: clk, ld, clr
  Adder #(.width(16)) adder_1 (.a(16'h1), .b(register_1_q), .out(adder_1_out));  // open: cin, cout
  Register #(.width(16), .Select("low")) register_1 (
    .D(adder_1_out), .Q(register_1_q), .clk(and_2_out), .clr(RESET_INST));  // open: en

  // Other names for the same wires on the sheet: ADDRESS[31:0] = out_12; IN_REGISTER[3:0] = out_17;
  //   OPCODE[3:0] = out_20; OPCODE_R[3:0] = out_22; OPCODE_ULA[3:0] = out_21; R1_R[31:0] = out_4;
  //   R1_ULA[31:0] = out_3; R2_R[31:0] = out_6; R2_ULA[31:0] = out_5; RESULT[31:0] = out_8; RS_R[31:0] = out_10;
  //   RS_ULA[31:0] = out_9; T1_R[3:0] = out_14; T1_ULA[3:0] = out_13; T2_R[3:0] = out_16; T2_ULA[3:0] = out_15;
  //   TS_R[3:0] = out_19; TS_ULA[3:0] = out_18

  // Notes on the sheet:
  //   RESULT OF INSTRUCTIONS
  //   ULA PIPELINE
  //   REGISTER PIPELINE
  //   TOTAL DE CLOCKS
endmodule

module ULA (
  input  [31:0] R1,
  input  [31:0] R2,
  input  [3:0] in_3,
  input  [31:0] RS,
  output [31:0] RESULT,
  output STATEMENT_IS_TRUE
);

  wire not_1_out, or_2_out, specialcode_1_if_equal, specialcode_1_if_not_equal;
  wire [31:0] adder_1_out, and_1_out, divider_1_out, multiplexer_1_out, multiplier_1_out, or_1_out,
       subtractor_1_out;

  specialCode specialcode_1 (
    .IS_SPECIAL(1'b1), .OPCODE(in_3), .IF_EQUAL(specialcode_1_if_equal),
    .IF_NOT_EQUAL(specialcode_1_if_not_equal));  // open: LI, SW, LW, JUMP
  Adder #(.width(32)) adder_1 (.a(R1), .b(R2), .out(adder_1_out));  // open: cin, cout
  Subtractor #(.width(32)) subtractor_1 (.a(R1), .b(R2), .out(subtractor_1_out));  // open: bin, bout
  Multiplier #(.width(32)) multiplier_1 (.a(R1), .b(R2), .out(multiplier_1_out));  // open: cin, cout
  Divider #(.width(32)) divider_1 (.a(R1), .b(R2), .out(divider_1_out));  // open: upper, rem
  assign or_1_out = R1 | R2;  // OR_Gate or_1, 32 bits wide
  assign and_1_out = R1 & R2;  // AND_Gate and_1, 32 bits wide
  not not_1 (not_1_out, in_3[3]);
  IF_STATES if_states_1 (
    .in_1(R1), .in_2(R2), .OP(specialcode_1_if_not_equal), .IS_A_IF_STATEMENT(or_2_out),
    .out_5(STATEMENT_IS_TRUE));
  Multiplexer #(.select(3), .width(32)) multiplexer_1 (
    .in0(adder_1_out), .in1(subtractor_1_out), .in2(multiplier_1_out), .in3(divider_1_out), .in4(or_1_out),
    .in5(and_1_out), .out(multiplexer_1_out), .sel(in_3[2:0]), .en(not_1_out));  // open: in6, in7
  or or_2 (or_2_out, specialcode_1_if_equal, specialcode_1_if_not_equal);
  MUX_ULA mux_ula_1 (.RS_ORIGINAL(RS), .AFTER_OP(multiplexer_1_out), .OPCODE(not_1_out), .RESULT(RESULT));
endmodule

module Registradores (
  input  [3:0] in_1,
  input  [3:0] in_2,
  input  [3:0] Register_Saver,
  input  TO_SAVE,
  input  [31:0] in_5,
  input  in_6,
  input  [3:0] in_7,
  output [31:0] R1,
  output [31:0] R2,
  output [31:0] RD
);

  wire if_equal_1_out_3, if_equal_1_out_4, if_equal_1_out_5, if_equal_1_out_6, if_equal_1_out_7,
       if_equal_1_out_8, if_equal_1_out_9, if_equal_1_out_10, if_equal_1_out_11, if_equal_1_out_12,
       if_equal_1_out_13, if_equal_1_out_14, if_equal_1_out_15;
  wire [31:0] demultiplexer_1_out1, demultiplexer_1_out2, demultiplexer_1_out3, demultiplexer_1_out4,
       demultiplexer_1_out5, demultiplexer_1_out6, demultiplexer_1_out7, demultiplexer_1_out8,
       demultiplexer_1_out9, demultiplexer_1_out10, demultiplexer_1_out11, demultiplexer_1_out12,
       demultiplexer_1_out13, register_1_q, register_2_q, register_3_q, register_4_q, register_5_q,
       register_6_q, register_7_q, register_8_q, register_9_q, register_10_q, register_11_q, register_12_q,
       register_13_q;

  Demultiplexer #(.select(4), .width(32)) demultiplexer_1 (
    .out1(demultiplexer_1_out1), .out2(demultiplexer_1_out2), .out3(demultiplexer_1_out3),
    .out4(demultiplexer_1_out4), .out5(demultiplexer_1_out5), .out6(demultiplexer_1_out6),
    .out7(demultiplexer_1_out7), .out8(demultiplexer_1_out8), .out9(demultiplexer_1_out9),
    .out10(demultiplexer_1_out10), .out11(demultiplexer_1_out11), .out12(demultiplexer_1_out12),
    .out13(demultiplexer_1_out13), .in(in_5), .sel(Register_Saver), .en(TO_SAVE));  // open: out0, out14, out15
  If_Equal if_equal_1 (
    .in_1(Register_Saver), .out_3(if_equal_1_out_3), .out_4(if_equal_1_out_4), .out_5(if_equal_1_out_5),
    .out_6(if_equal_1_out_6), .out_7(if_equal_1_out_7), .out_8(if_equal_1_out_8), .out_9(if_equal_1_out_9),
    .out_10(if_equal_1_out_10), .out_11(if_equal_1_out_11), .out_12(if_equal_1_out_12),
    .out_13(if_equal_1_out_13), .out_14(if_equal_1_out_14), .out_15(if_equal_1_out_15));  // open: out_2
  Register #(.width(32), .Select("low")) register_1 (
    .D(demultiplexer_1_out1), .en(if_equal_1_out_3), .Q(register_1_q), .clk(in_6));  // open: clr
  Register #(.width(32), .Select("low")) register_2 (
    .D(demultiplexer_1_out2), .en(if_equal_1_out_4), .Q(register_2_q), .clk(in_6));  // open: clr
  Register #(.width(32), .Select("low")) register_3 (
    .D(demultiplexer_1_out3), .en(if_equal_1_out_5), .Q(register_3_q), .clk(in_6));  // open: clr
  Register #(.width(32), .Select("low")) register_4 (
    .D(demultiplexer_1_out4), .en(if_equal_1_out_6), .Q(register_4_q), .clk(in_6));  // open: clr
  Register #(.width(32), .Select("low")) register_5 (
    .D(demultiplexer_1_out5), .en(if_equal_1_out_7), .Q(register_5_q), .clk(in_6));  // open: clr
  Register #(.width(32), .Select("low")) register_6 (
    .D(demultiplexer_1_out6), .en(if_equal_1_out_8), .Q(register_6_q), .clk(in_6));  // open: clr
  Register #(.width(32), .Select("low")) register_7 (
    .D(demultiplexer_1_out7), .en(if_equal_1_out_9), .Q(register_7_q), .clk(in_6));  // open: clr
  Register #(.width(32), .Select("low")) register_8 (
    .D(demultiplexer_1_out8), .en(if_equal_1_out_10), .Q(register_8_q), .clk(in_6));  // open: clr
  Register #(.width(32), .Select("low")) register_9 (
    .D(demultiplexer_1_out9), .en(if_equal_1_out_11), .Q(register_9_q), .clk(in_6));  // open: clr
  Register #(.width(32), .Select("low")) register_10 (
    .D(demultiplexer_1_out10), .en(if_equal_1_out_12), .Q(register_10_q), .clk(in_6));  // open: clr
  Register #(.width(32), .Select("low")) register_11 (
    .D(demultiplexer_1_out11), .en(if_equal_1_out_13), .Q(register_11_q), .clk(in_6));  // open: clr
  Register #(.width(32), .Select("low")) register_12 (
    .D(demultiplexer_1_out12), .en(if_equal_1_out_14), .Q(register_12_q), .clk(in_6));  // open: clr
  Register #(.width(32), .Select("low")) register_13 (
    .D(demultiplexer_1_out13), .en(if_equal_1_out_15), .Q(register_13_q), .clk(in_6));  // open: clr
  Multiplexer #(.select(4), .width(32)) multiplexer_1 (
    .in0({32{1'b0}}), .in1(register_1_q), .in2(register_2_q), .in3(register_3_q), .in4(register_4_q),
    .in5(register_5_q), .in6(register_6_q), .in7(register_7_q), .in8(register_8_q), .in9(register_9_q),
    .in10(register_10_q), .in11(register_11_q), .in12(register_12_q), .in13(register_13_q), .out(R1),
    .sel(in_1));  // open: in14, in15, en
  Multiplexer #(.select(4), .width(32)) multiplexer_2 (
    .in0({32{1'b0}}), .in1(register_1_q), .in2(register_2_q), .in3(register_3_q), .in4(register_4_q),
    .in5(register_5_q), .in6(register_6_q), .in7(register_7_q), .in8(register_8_q), .in9(register_9_q),
    .in10(register_10_q), .in11(register_11_q), .in12(register_12_q), .in13(register_13_q), .out(R2),
    .sel(in_2));  // open: in14, in15, en
  Multiplexer #(.select(4), .width(32)) multiplexer_3 (
    .in0({32{1'b0}}), .in1(register_1_q), .in2(register_2_q), .in3(register_3_q), .in4(register_4_q),
    .in5(register_5_q), .in6(register_6_q), .in7(register_7_q), .in8(register_8_q), .in9(register_9_q),
    .in10(register_10_q), .in11(register_11_q), .in12(register_12_q), .in13(register_13_q), .out(RD),
    .sel(in_7));  // open: in14, in15, en
endmodule

module If_Equal (
  input  [3:0] in_1,
  output out_2,
  output out_3,
  output out_4,
  output out_5,
  output out_6,
  output out_7,
  output out_8,
  output out_9,
  output out_10,
  output out_11,
  output out_12,
  output out_13,
  output out_14,
  output out_15
);

  Comparator #(.width(4)) comparator_1 (.a(4'b0000), .b(in_1), .eq(out_2));  // open: gt, lt
  Comparator #(.width(4)) comparator_2 (.a(4'b0001), .b(in_1), .eq(out_3));  // open: gt, lt
  Comparator #(.width(4)) comparator_3 (.a(4'b0010), .b(in_1), .eq(out_4));  // open: gt, lt
  Comparator #(.width(4)) comparator_4 (.a(4'b0011), .b(in_1), .eq(out_5));  // open: gt, lt
  Comparator #(.width(4)) comparator_5 (.a(4'b0100), .b(in_1), .eq(out_6));  // open: gt, lt
  Comparator #(.width(4)) comparator_6 (.a(4'b0101), .b(in_1), .eq(out_7));  // open: gt, lt
  Comparator #(.width(4)) comparator_7 (.a(4'b0110), .b(in_1), .eq(out_8));  // open: gt, lt
  Comparator #(.width(4)) comparator_8 (.a(4'b0111), .b(in_1), .eq(out_9));  // open: gt, lt
  Comparator #(.width(4)) comparator_9 (.a(4'b1000), .b(in_1), .eq(out_10));  // open: gt, lt
  Comparator #(.width(4)) comparator_10 (.a(4'b1001), .b(in_1), .eq(out_11));  // open: gt, lt
  Comparator #(.width(4)) comparator_11 (.a(4'b1010), .b(in_1), .eq(out_12));  // open: gt, lt
  Comparator #(.width(4)) comparator_12 (.a(4'b1011), .b(in_1), .eq(out_13));  // open: gt, lt
  Comparator #(.width(4)) comparator_13 (.a(4'b1100), .b(in_1), .eq(out_14));  // open: gt, lt
  Comparator #(.width(4)) comparator_14 (.a(4'b1101), .b(in_1), .eq(out_15));  // open: gt, lt
endmodule

module codeReader (
  input  [31:0] in_1,
  input  kill_everyone,
  output [3:0] OP_CODE,
  output LI,
  output SW,
  output LW,
  output JUMP,
  output [3:0] R1,
  output IF_EQUAL,
  output [3:0] R2,
  output IF_NOT_EQUAL,
  output [3:0] R3,
  output [31:0] IMEDIATTE_ADDRESS,
  output out_14
);

  extend_16_32 extend_16_32_1 (.in_1(in_1[15:0]), .out_2(IMEDIATTE_ADDRESS));
  specialCode specialcode_1 (
    .IS_SPECIAL(in_1[31]), .OPCODE(in_1[31:28]), .LI(LI), .SW(SW), .LW(LW), .JUMP(JUMP), .IF_EQUAL(IF_EQUAL),
    .IF_NOT_EQUAL(IF_NOT_EQUAL));

  assign OP_CODE = in_1[31:28];
  assign out_14 = kill_everyone;
  assign R1 = in_1[27:24];
  assign R2 = in_1[23:20];
  assign R3 = in_1[19:16];
endmodule

module extend_16_32 (
  input  [15:0] in_1,
  output [31:0] out_2
);

  assign out_2 = {{16{1'b0}}, in_1};  // Bit_Extender bit_extender_1
endmodule

module specialCode (
  input  IS_SPECIAL,
  input  [3:0] OPCODE,
  output LI,
  output SW,
  output LW,
  output JUMP,
  output IF_EQUAL,
  output IF_NOT_EQUAL
);

  wire comparator_1_eq, comparator_2_eq, comparator_3_eq, comparator_4_eq, comparator_5_eq, comparator_6_eq;

  Comparator #(.width(4)) comparator_1 (.a(OPCODE), .b(4'b1000), .eq(comparator_1_eq));  // open: gt, lt
  Comparator #(.width(4)) comparator_2 (.a(OPCODE), .b(4'b1001), .eq(comparator_2_eq));  // open: gt, lt
  Comparator #(.width(4)) comparator_3 (.a(OPCODE), .b(4'b1010), .eq(comparator_3_eq));  // open: gt, lt
  Comparator #(.width(4)) comparator_4 (.a(OPCODE), .b(4'b1011), .eq(comparator_4_eq));  // open: gt, lt
  Comparator #(.width(4)) comparator_5 (.a(OPCODE), .b(4'b1100), .eq(comparator_5_eq));  // open: gt, lt
  Comparator #(.width(4)) comparator_6 (.a(OPCODE), .b(4'b1101), .eq(comparator_6_eq));  // open: gt, lt
  and and_1 (LI, IS_SPECIAL, comparator_1_eq);
  and and_2 (SW, IS_SPECIAL, comparator_2_eq);
  and and_3 (LW, IS_SPECIAL, comparator_3_eq);
  and and_4 (JUMP, IS_SPECIAL, comparator_4_eq);
  and and_5 (IF_EQUAL, IS_SPECIAL, comparator_5_eq);
  and and_6 (IF_NOT_EQUAL, IS_SPECIAL, comparator_6_eq);
endmodule

module JUMPER (
  input  CONDITION_IS_TRUE,
  input  HAVE_A_CONDITION,
  input  WHANT_TO_JUMP,
  output WILL_JUMP
);

  wire and_1_out, multiplexer_1_out;

  and and_1 (and_1_out, CONDITION_IS_TRUE, HAVE_A_CONDITION);
  Multiplexer multiplexer_1 (
    .in0(WHANT_TO_JUMP), .in1(1'b0), .out(multiplexer_1_out), .sel(HAVE_A_CONDITION));  // open: en
  or or_1 (WILL_JUMP, and_1_out, multiplexer_1_out);
endmodule

module IF_STATES (
  input  [31:0] in_1,
  input  [31:0] in_2,
  input  OP,
  input  IS_A_IF_STATEMENT,
  output out_5
);

  wire comparator_1_eq, comparator_1_lt, or_1_out;

  Comparator #(.width(32)) comparator_1 (.a(in_1), .b(in_2), .eq(comparator_1_eq), .lt(comparator_1_lt));  // open: gt
  or or_1 (or_1_out, comparator_1_eq, comparator_1_lt);
  Multiplexer multiplexer_1 (.in0(comparator_1_eq), .in1(or_1_out), .out(out_5), .sel(OP), .en(IS_A_IF_STATEMENT));
endmodule

module COUNTER_INSTRUCTION (
  input  [15:0] ADDRESS_CURRENT,
  input  CONDITION_IS_TRUE,
  input  IS_ACTIVE,
  input  STATE_TYPE_1,
  input  STATE_TYPE_2,
  input  [31:0] ADDRESS_JUMP,
  input  WHANT_TO_JUMP,
  input  STOP_PROCESS,
  output [15:0] NEXT_ADDRESS,
  output NEED_TO_FLUSH_MEMORY
);

  wire jumper_1_will_jump, multiplexer_1_out, or_1_out;
  wire [15:0] adder_1_out, multiplexer_2_out, multiplexer_3_out, short_32_16_1_out_2;

  or or_1 (or_1_out, STATE_TYPE_1, STATE_TYPE_2);
  Multiplexer multiplexer_1 (.in0(1'b0), .in1(CONDITION_IS_TRUE), .out(multiplexer_1_out), .sel(or_1_out));  // open: en
  Multiplexer #(.width(16)) multiplexer_2 (
    .in0(16'h1), .in1({16{1'b0}}), .out(multiplexer_2_out), .sel(STOP_PROCESS));  // open: en
  JUMPER jumper_1 (
    .CONDITION_IS_TRUE(multiplexer_1_out), .HAVE_A_CONDITION(or_1_out), .WHANT_TO_JUMP(WHANT_TO_JUMP),
    .WILL_JUMP(jumper_1_will_jump));
  Adder #(.width(16)) adder_1 (.a(ADDRESS_CURRENT), .b(multiplexer_2_out), .out(adder_1_out));  // open: cin, cout
  short_32_16 short_32_16_1 (.in_1(ADDRESS_JUMP), .out_2(short_32_16_1_out_2));
  Multiplexer #(.width(16)) multiplexer_3 (
    .in0(adder_1_out), .in1(short_32_16_1_out_2), .out(multiplexer_3_out), .sel(jumper_1_will_jump));  // open: en
  buf and_1 (NEED_TO_FLUSH_MEMORY, jumper_1_will_jump);  // AND_Gate
  Multiplexer #(.width(16)) multiplexer_4 (
    .in0(adder_1_out), .in1(multiplexer_3_out), .out(NEXT_ADDRESS), .sel(IS_ACTIVE));  // open: en
endmodule

module SAVE_IN_REGISTER (
  input  NORMAL_OP,
  input  LI,
  input  LW,
  input  [31:0] FROM_ULA,
  input  [31:0] IMMEDIATE,
  input  [31:0] FROM_MEMORY,
  output TO_SAVE,
  output [31:0] out_8
);

  wire undriven;

  or or_1 (TO_SAVE, NORMAL_OP, LI, LW);
  Multiplexer #(.select(2), .width(32)) multiplexer_1 (
    .in0(FROM_ULA), .in1(IMMEDIATE), .in2(FROM_MEMORY), .out(out_8), .sel({LW, LI}), .en(undriven));  // open: in3
endmodule

module short_32_16 (
  input  [31:0] in_1,
  output [15:0] out_2
);

  Bit_Extender #(.in_width(32), .\type ("input")) bit_extender_1 (.in(in_1), .out(out_2));  // open: extend
endmodule

module PipeLine_Main (
  input  RESET_INST,
  output [31:0] out_2,
  output [31:0] out_3,
  output [31:0] out_4,
  output [31:0] out_5,
  output [31:0] out_6,
  output [31:0] out_7,
  output [31:0] out_8,
  output [31:0] out_9,
  output [3:0] out_10,
  output [3:0] out_11,
  output [3:0] out_12,
  output [3:0] out_13,
  output [3:0] out_14,
  output [3:0] out_15,
  output [3:0] out_16,
  output [3:0] out_17,
  output [3:0] out_18,
  output [3:0] out_19
);

  wire clock_1_out, codereader_1_if_equal, codereader_1_if_not_equal, codereader_1_jump, codereader_1_li,
       codereader_1_lw, codereader_1_out_14, codereader_1_sw, counter_instruction_1_need_to_flush_memory,
       handle_errors_1_p9, handle_errors_1_p13, handle_errors_1_p14, handle_errors_1_p15,
       instruction_position_1_need_to_flush, or_1_out, pipeline_1_1_if_equal_2,
       pipeline_1_1_if_less_or_equal_2, pipeline_1_1_is_enabled, pipeline_1_1_jump_2,
       pipeline_1_1_kill_process_2, pipeline_1_1_li_2, pipeline_1_1_lw_2, pipeline_1_1_sw_2,
       pipeline_2_1_if_equal_2, pipeline_2_1_if_less_or_equal_2, pipeline_2_1_jump_2, pipeline_2_1_sw_2,
       pipeline_2_1_true_statement_2, pipeline_register_1_if_equal_2, pipeline_register_1_if_less_or_equal_2,
       pipeline_register_1_is_enabled, pipeline_register_1_jump_2, pipeline_register_1_li_2,
       pipeline_register_1_lw_2, pipeline_register_1_sw_2, save_in_register_1_p6, ula_1_statement_is_true,
       undriven;
  wire [3:0] codereader_1_op_code, codereader_1_r1, codereader_1_r2, codereader_1_r3, handle_errors_1_p11,
       pipeline_1_1_opcode_2, pipeline_1_1_rd_2, pipeline_1_1_rt2_2, pipeline_1_1_rt_2,
       pipeline_2_1_opcode_2, pipeline_register_1_opcode_2, pipeline_register_1_t1_2,
       pipeline_register_1_t2_2, pipeline_register_1_ts_2;
  wire [15:0] counter_instruction_1_next_address, instruction_position_1_out_6;
  wire [31:0] codereader_1_imediatte_address, handle_errors_1_p7, handle_errors_1_p8, handle_errors_1_p10,
       handle_errors_1_p12, pipeline_1_1_integer_2, pipeline_2_1_integer_2, pipeline_2_1_rd_2,
       pipeline_2_1_rt_2, pipeline_register_1_integer_2, pipeline_register_1_rd_2, pipeline_register_1_rt2,
       pipeline_register_1_rt_3, ram_1_data, registradores_1_r1, registradores_1_r2, registradores_1_rd,
       ula_1_result;

  codeReader codereader_1 (
    .in_1(ram_1_data), .OP_CODE(codereader_1_op_code), .R1(codereader_1_r1), .R2(codereader_1_r2),
    .R3(codereader_1_r3), .IMEDIATTE_ADDRESS(codereader_1_imediatte_address), .LI(codereader_1_li),
    .SW(codereader_1_sw), .LW(codereader_1_lw), .JUMP(codereader_1_jump), .IF_EQUAL(codereader_1_if_equal),
    .IF_NOT_EQUAL(codereader_1_if_not_equal), .kill_everyone(instruction_position_1_need_to_flush),
    .out_14(codereader_1_out_14));
  Pipeline_1 pipeline_1_1 (
    .OPCODE(codereader_1_op_code), .RT(codereader_1_r1), .RT2(codereader_1_r2), .RD(codereader_1_r3),
    .LI(codereader_1_li), .SW(codereader_1_sw), .LW(codereader_1_lw), .JUMP(codereader_1_jump),
    .IF_EQUAL(codereader_1_if_equal), .IF_LESS_OR_EQUAL(codereader_1_if_not_equal), .CLOCK(clock_1_out),
    .OPCODE_2(pipeline_1_1_opcode_2), .RT_2(pipeline_1_1_rt_2), .RT2_2(pipeline_1_1_rt2_2),
    .RD_2(pipeline_1_1_rd_2), .LI_2(pipeline_1_1_li_2), .SW_2(pipeline_1_1_sw_2), .LW_2(pipeline_1_1_lw_2),
    .JUMP_2(pipeline_1_1_jump_2), .IF_EQUAL_2(pipeline_1_1_if_equal_2),
    .IF_LESS_OR_EQUAL_2(pipeline_1_1_if_less_or_equal_2), .INTEGER(codereader_1_imediatte_address),
    .INTEGER_2(pipeline_1_1_integer_2), .IS_ENABLED(pipeline_1_1_is_enabled), .RESET(or_1_out),
    .KILL_PROCESS(codereader_1_out_14), .KILL_PROCESS_2(pipeline_1_1_kill_process_2));
  Registradores registradores_1 (
    .in_1(pipeline_1_1_rt_2), .in_2(pipeline_1_1_rt2_2), .R1(registradores_1_r1), .R2(registradores_1_r2),
    .in_5(handle_errors_1_p12), .in_6(clock_1_out), .in_7(pipeline_1_1_rd_2), .RD(registradores_1_rd),
    .TO_SAVE(undriven), .Register_Saver(handle_errors_1_p11));
  REGISTERS_OUTPUT registers_output_1 (
    .OPCODE(pipeline_1_1_opcode_2), .R1(registradores_1_r1), .R2(registradores_1_r2),
    .RD(registradores_1_rd), .T1(pipeline_1_1_rt_2), .T2(pipeline_1_1_rt2_2), .TS(pipeline_1_1_rd_2),
    .OPCODE_2(out_19), .R1_2(out_3), .R2_2(out_6), .RD_2(out_9), .T1_2(out_13), .T2_2(out_15), .TS_2(out_17));
  or or_1 (or_1_out, RESET_INST, pipeline_1_1_kill_process_2);
  PIPELINE_REGISTER pipeline_register_1 (
    .RT(registradores_1_r1), .RD(registradores_1_rd), .LI(pipeline_1_1_li_2), .SW(pipeline_1_1_sw_2),
    .LW(pipeline_1_1_lw_2), .JUMP(pipeline_1_1_jump_2), .IF_EQUAL(pipeline_1_1_if_equal_2),
    .IF_LESS_OR_EQUAL(pipeline_1_1_if_less_or_equal_2), .INTEGER(pipeline_1_1_integer_2),
    .CLOCK(clock_1_out), .RT_3(pipeline_register_1_rt_3), .RD_2(pipeline_register_1_rd_2),
    .LI_2(pipeline_register_1_li_2), .SW_2(pipeline_register_1_sw_2), .LW_2(pipeline_register_1_lw_2),
    .JUMP_2(pipeline_register_1_jump_2), .IF_EQUAL_2(pipeline_register_1_if_equal_2),
    .IF_LESS_OR_EQUAL_2(pipeline_register_1_if_less_or_equal_2), .INTEGER_2(pipeline_register_1_integer_2),
    .RT_2(registradores_1_r2), .RT2(pipeline_register_1_rt2), .T1(pipeline_1_1_rt_2),
    .T1_2(pipeline_register_1_t1_2), .T2(pipeline_1_1_rt2_2), .T2_2(pipeline_register_1_t2_2),
    .OPCODE(pipeline_1_1_opcode_2), .OPCODE_2(pipeline_register_1_opcode_2), .RESET(or_1_out),
    .IS_ABLE(pipeline_1_1_is_enabled), .IS_ENABLED(pipeline_register_1_is_enabled), .TS(pipeline_1_1_rd_2),
    .TS_2(pipeline_register_1_ts_2));
  // HANDLE_ERRORS handle_errors_1: pin names not known; wires that end beside it: pipeline_register_1_t1_2, pipeline_register_1_t2_2, pipeline_register_1_ts_2, pipeline_register_1_rt_3, pipeline_register_1_rt2, pipeline_register_1_rd_2, handle_errors_1_p7, handle_errors_1_p8, handle_errors_1_p9, handle_errors_1_p10, handle_errors_1_p11, handle_errors_1_p12, handle_errors_1_p13, handle_errors_1_p14, handle_errors_1_p15
  Clock clock_1 (.out(clock_1_out));
  ULA ula_1 (
    .R1(handle_errors_1_p7), .R2(handle_errors_1_p8), .in_3(pipeline_register_1_opcode_2),
    .RESULT(ula_1_result), .STATEMENT_IS_TRUE(ula_1_statement_is_true), .RS(handle_errors_1_p10));
  ULA_OUTPUT ula_output_1 (
    .OPCODE(pipeline_register_1_opcode_2), .R1(handle_errors_1_p7), .R2(handle_errors_1_p8),
    .RD(ula_1_result), .T1(pipeline_register_1_t1_2), .T2(pipeline_register_1_t2_2),
    .TS(pipeline_register_1_ts_2), .OPCODE_2(out_18), .R1_2(out_2), .R2_2(out_5), .RD_2(out_8),
    .T1_2(out_12), .T2_2(out_14), .TS_2(out_16));
  COUNTER_INSTRUCTION counter_instruction_1 (
    .ADDRESS_CURRENT(instruction_position_1_out_6), .CONDITION_IS_TRUE(pipeline_2_1_true_statement_2),
    .STATE_TYPE_1(pipeline_2_1_if_less_or_equal_2), .STATE_TYPE_2(pipeline_2_1_if_equal_2),
    .ADDRESS_JUMP(pipeline_2_1_rd_2), .WHANT_TO_JUMP(pipeline_2_1_jump_2), .IS_ACTIVE(handle_errors_1_p9),
    .NEED_TO_FLUSH_MEMORY(counter_instruction_1_need_to_flush_memory),
    .NEXT_ADDRESS(counter_instruction_1_next_address));  // open: STOP_PROCESS
  instruction_position instruction_position_1 (
    .in_1(counter_instruction_1_next_address), .clock(clock_1_out),
    .FLUSH_MEMORY(counter_instruction_1_need_to_flush_memory), .out_6(instruction_position_1_out_6),
    .NEED_TO_FLUSH(instruction_position_1_need_to_flush), .RESET(RESET_INST));  // open: isStopProcess
  OUTPUT output_1 (
    .OPCODE(pipeline_2_1_opcode_2), .RD(handle_errors_1_p12), .TS(handle_errors_1_p11),
    .ADDRESS(pipeline_2_1_rt_2), .OPCODE_2(out_11), .RESULT(out_4), .IN_THIS_REGISTER(out_10),
    .ADDRESS_2(out_7));
  Pipeline_2 pipeline_2_1 (
    .TRUE_STATEMENT(ula_1_statement_is_true), .RT(handle_errors_1_p7), .RD(ula_1_result),
    .LI(pipeline_register_1_li_2), .SW(pipeline_register_1_sw_2), .LW(pipeline_register_1_lw_2),
    .JUMP(pipeline_register_1_jump_2), .IF_EQUAL(pipeline_register_1_if_equal_2),
    .IF_LESS_OR_EQUAL(pipeline_register_1_if_less_or_equal_2), .CLOCK(clock_1_out),
    .INTEGER(pipeline_register_1_integer_2), .TRUE_STATEMENT_2(pipeline_2_1_true_statement_2),
    .RT_2(pipeline_2_1_rt_2), .RD_2(pipeline_2_1_rd_2), .LI_2(handle_errors_1_p14), .SW_2(pipeline_2_1_sw_2),
    .LW_2(handle_errors_1_p15), .JUMP_2(pipeline_2_1_jump_2), .IF_EQUAL_2(pipeline_2_1_if_equal_2),
    .IF_LESS_OR_EQUAL_2(pipeline_2_1_if_less_or_equal_2), .INTEGER_2(pipeline_2_1_integer_2),
    .T1(pipeline_register_1_t1_2), .TS(pipeline_register_1_ts_2), .TS_2(handle_errors_1_p11),
    .OPCODE(pipeline_register_1_opcode_2), .OPCODE_2(pipeline_2_1_opcode_2),
    .IS_ABLE(pipeline_register_1_is_enabled), .IS_ENABLED(handle_errors_1_p9), .RESET(or_1_out));  // open: T1_2
  RAM #(.addrWidth(16), .dataWidth(32), .Select("high"), .simpleMode("false")) ram_1 (
    .addr(instruction_position_1_out_6), .data(ram_1_data), .clk(clock_1_out));  // open: sel, ld, clr
  IS_ARITIMETIC is_aritimetic_1 (.in_1(pipeline_2_1_opcode_2), .IS_ARITIMETIC(handle_errors_1_p13));
  // SAVE_IN_REGISTER save_in_register_1: pin names not known; wires that end beside it: pipeline_2_1_rd_2, handle_errors_1_p14, handle_errors_1_p15, pipeline_2_1_integer_2, handle_errors_1_p15, save_in_register_1_p6, handle_errors_1_p15
  // Memory memory_1: pin names not known; wires that end beside it: pipeline_2_1_rd_2, pipeline_2_1_rt_2, clock_1_out, pipeline_2_1_sw_2, save_in_register_1_p6

  // Other names for the same wires on the sheet: ADDRESS[31:0] = out_7; IN_REGISTER[3:0] = out_10;
  //   OPCODE[3:0] = out_11; OPCODE_R[3:0] = out_19; OPCODE_ULA[3:0] = out_18; R1_R[31:0] = out_3;
  //   R1_ULA[31:0] = out_2; R2_R[31:0] = out_6; R2_ULA[31:0] = out_5; RESULT[31:0] = out_4; RS_R[31:0] = out_9;
  //   RS_ULA[31:0] = out_8; T1_R[3:0] = out_13; T1_ULA[3:0] = out_12; T2_R[3:0] = out_15; T2_ULA[3:0] = out_14;
  //   TS_R[3:0] = out_17; TS_ULA[3:0] = out_16

  // Notes on the sheet:
  //   RESULT OF INSTRUCTIONS
  //   ULA PIPELINE
  //   REGISTER PIPELINE
endmodule

module Pipeline_1 (
  input  [3:0] OPCODE,
  input  [3:0] RT,
  input  [3:0] RT2,
  input  [3:0] RD,
  input  LI,
  input  SW,
  input  LW,
  input  JUMP,
  input  IF_EQUAL,
  input  IF_LESS_OR_EQUAL,
  input  CLOCK,
  input  [31:0] INTEGER,
  input  KILL_PROCESS,
  input  RESET,
  output [3:0] OPCODE_2,
  output [3:0] RT_2,
  output [3:0] RT2_2,
  output [3:0] RD_2,
  output LI_2,
  output SW_2,
  output LW_2,
  output JUMP_2,
  output IF_EQUAL_2,
  output IF_LESS_OR_EQUAL_2,
  output [31:0] INTEGER_2,
  output KILL_PROCESS_2,
  output IS_ENABLED
);

  Register #(.width(4), .Select("low")) u_opcode (.D(OPCODE), .Q(OPCODE_2), .clk(CLOCK), .clr(RESET));  // open: en
  Register #(.width(4), .Select("low")) u_RT (.D(RT), .Q(RT_2), .clk(CLOCK), .clr(RESET));  // open: en
  Register #(.width(4), .Select("low")) u_RT_2 (.D(RT2), .Q(RT2_2), .clk(CLOCK), .clr(RESET));  // open: en
  Register #(.width(4), .Select("low")) RT_3 (.D(RD), .Q(RD_2), .clk(CLOCK), .clr(RESET));  // open: en
  Register #(.width(1), .Select("low")) u_LI (.D(LI), .Q(LI_2), .clk(CLOCK), .clr(RESET));  // open: en
  Register #(.width(1), .Select("low")) u_SW (.D(SW), .Q(SW_2), .clk(CLOCK), .clr(RESET));  // open: en
  Register #(.width(1), .Select("low")) KILL (
    .D(KILL_PROCESS), .Q(KILL_PROCESS_2), .clk(CLOCK), .clr(RESET));  // open: en
  Register #(.width(1), .Select("low")) u_LW (.D(LW), .Q(LW_2), .clk(CLOCK), .clr(RESET));  // open: en
  Register #(.width(1), .Select("low")) u_JUMP (.D(JUMP), .Q(JUMP_2), .clk(CLOCK), .clr(RESET));  // open: en
  Register #(.width(1), .Select("low")) u_IF_EQUAL (
    .D(IF_EQUAL), .Q(IF_EQUAL_2), .clk(CLOCK), .clr(RESET));  // open: en
  Register #(.width(1), .Select("low")) u_IF_LESS_OR_EQUAL (
    .D(IF_LESS_OR_EQUAL), .Q(IF_LESS_OR_EQUAL_2), .clk(CLOCK), .clr(RESET));  // open: en
  Register #(.width(32), .Select("low")) u_INTEGER (.D(INTEGER), .Q(INTEGER_2), .clk(CLOCK), .clr(RESET));  // open: en
  Register #(.width(1), .Select("low")) register_1 (.D(CLOCK), .Q(IS_ENABLED), .clk(CLOCK), .clr(RESET));  // open: en
endmodule

module Pipiline_JUMPS_IFS (
  input  TRUE_STATEMENT,
  input  JUMP,
  input  IF_EQUAL,
  input  CLOCK,
  input  IF_LESS_OR_EQUAL,
  input  [31:0] ADDRESS_JUMP,
  output TRUE_STATEMENT_2,
  output JUMP_2,
  output IF_EQUAL_2,
  output IF_LESS_OR_EQUAL_2,
  output [31:0] INTEGER
);

  Register #(.width(1), .Select("low")) u_JUMP (
    .D(TRUE_STATEMENT), .Q(TRUE_STATEMENT_2), .clk(CLOCK));  // open: en, clr
  Register #(.width(1), .Select("low")) u_JUMP_2 (.D(JUMP), .Q(JUMP_2), .clk(CLOCK));  // open: en, clr
  Register #(.width(1), .Select("low")) u_IF_EQUAL (.D(IF_EQUAL), .Q(IF_EQUAL_2), .clk(CLOCK));  // open: en, clr
  Register #(.width(1), .Select("low")) u_IF_LESS_OR_EQUAL (
    .D(IF_LESS_OR_EQUAL), .Q(IF_LESS_OR_EQUAL_2), .clk(CLOCK));  // open: en, clr
  Register #(.width(32), .Select("low")) u_INTEGER (.D(ADDRESS_JUMP), .Q(INTEGER), .clk(CLOCK));  // open: en, clr
endmodule

module Pipeline_2 (
  input  [3:0] OPCODE,
  input  TRUE_STATEMENT,
  input  [31:0] RT,
  input  [31:0] RD,
  input  LI,
  input  SW,
  input  LW,
  input  JUMP,
  input  IF_EQUAL,
  input  IF_LESS_OR_EQUAL,
  input  [31:0] INTEGER,
  input  [3:0] T1,
  input  [3:0] TS,
  input  CLOCK,
  input  IS_ABLE,
  input  RESET,
  output [3:0] OPCODE_2,
  output TRUE_STATEMENT_2,
  output [31:0] RT_2,
  output [31:0] RD_2,
  output LI_2,
  output SW_2,
  output LW_2,
  output JUMP_2,
  output IF_EQUAL_2,
  output IF_LESS_OR_EQUAL_2,
  output [31:0] INTEGER_2,
  output [3:0] T1_2,
  output [3:0] TS_2,
  output IS_ENABLED
);

  wire IF_EQUAL_q, IF_LESS_OR_EQUAL_2_q, JUMP_q, LI_q, LW_q, not_1_out, SW_q, TRUE_q;
  wire [3:0] INTEGER_2_q, INTEGER_3_q, opcode_q;
  wire [31:0] INTEGER_q, RT_2_q, RT_q;

  Register #(.width(4), .Select("low")) u_opcode (.D(OPCODE), .Q(opcode_q), .clk(CLOCK), .clr(RESET));  // open: en
  Register #(.width(1), .Select("low")) TRUE (.D(TRUE_STATEMENT), .Q(TRUE_q), .clk(CLOCK), .clr(RESET));  // open: en
  Register #(.width(32), .Select("low")) u_RT (.D(RT), .Q(RT_q), .clk(CLOCK), .clr(RESET));  // open: en
  Register #(.width(32), .Select("low")) u_RT_2 (.D(RD), .Q(RT_2_q), .clk(CLOCK), .clr(RESET));  // open: en
  Register #(.width(1), .Select("low")) u_LI (.D(LI), .Q(LI_q), .clk(CLOCK), .clr(RESET));  // open: en
  Register #(.width(1), .Select("low")) u_SW (.D(SW), .Q(SW_q), .clk(CLOCK), .clr(RESET));  // open: en
  Register #(.width(1), .Select("low")) u_LW (.D(LW), .Q(LW_q), .clk(CLOCK), .clr(RESET));  // open: en
  Register #(.width(1), .Select("low")) u_JUMP (.D(JUMP), .Q(JUMP_q), .clk(CLOCK), .clr(RESET));  // open: en
  Register #(.width(1), .Select("low")) u_IF_LESS_OR_EQUAL (
    .D(IS_ABLE), .en(IS_ABLE), .Q(IS_ENABLED), .clk(CLOCK), .clr(RESET));
  Register #(.width(1), .Select("low")) u_IF_EQUAL (
    .D(IF_EQUAL), .Q(IF_EQUAL_q), .clk(CLOCK), .clr(RESET));  // open: en
  Register #(.width(1), .Select("low")) u_IF_LESS_OR_EQUAL_2 (
    .D(IF_LESS_OR_EQUAL), .Q(IF_LESS_OR_EQUAL_2_q), .clk(CLOCK), .clr(RESET));  // open: en
  Register #(.width(32), .Select("low")) u_INTEGER (.D(INTEGER), .Q(INTEGER_q), .clk(CLOCK), .clr(RESET));  // open: en
  Register #(.width(4), .Select("low")) u_INTEGER_2 (.D(T1), .Q(INTEGER_2_q), .clk(CLOCK), .clr(RESET));  // open: en
  Register #(.width(4), .Select("low")) INTEGER_3 (.D(TS), .Q(INTEGER_3_q), .clk(CLOCK), .clr(RESET));  // open: en
  not not_1 (not_1_out, IS_ENABLED);
  Multiplexer #(.width(4)) multiplexer_1 (.in0(INTEGER_2_q), .out(T1_2), .sel(not_1_out));  // open: in1, en
  Multiplexer #(.width(4)) multiplexer_2 (.in0(INTEGER_3_q), .out(TS_2), .sel(not_1_out));  // open: in1, en
  Multiplexer #(.width(4)) multiplexer_3 (.in0(opcode_q), .out(OPCODE_2), .sel(not_1_out));  // open: in1, en
  Multiplexer multiplexer_4 (.in0(TRUE_q), .out(TRUE_STATEMENT_2), .sel(not_1_out));  // open: in1, en
  Multiplexer #(.width(32)) multiplexer_5 (.in0(RT_q), .out(RT_2), .sel(not_1_out));  // open: in1, en
  Multiplexer #(.width(32)) multiplexer_6 (.in0(RT_2_q), .out(RD_2), .sel(not_1_out));  // open: in1, en
  Multiplexer multiplexer_7 (.in0(LI_q), .out(LI_2), .sel(not_1_out));  // open: in1, en
  Multiplexer multiplexer_8 (.in0(SW_q), .out(SW_2), .sel(not_1_out));  // open: in1, en
  Multiplexer multiplexer_9 (.in0(LW_q), .out(LW_2), .sel(not_1_out));  // open: in1, en
  Multiplexer multiplexer_10 (.in0(JUMP_q), .out(JUMP_2), .sel(not_1_out));  // open: in1, en
  Multiplexer multiplexer_11 (.in0(IF_EQUAL_q), .out(IF_EQUAL_2), .sel(not_1_out));  // open: in1, en
  Multiplexer multiplexer_12 (.in0(IF_LESS_OR_EQUAL_2_q), .out(IF_LESS_OR_EQUAL_2), .sel(not_1_out));  // open: in1, en
  Multiplexer #(.width(32)) multiplexer_13 (.in0(INTEGER_q), .out(INTEGER_2), .sel(not_1_out));  // open: in1, en
endmodule

module PIPELINE_REGISTER (
  input  [3:0] OPCODE,
  input  [31:0] RT,
  input  [31:0] RT_2,
  input  [31:0] RD,
  input  LI,
  input  SW,
  input  LW,
  input  JUMP,
  input  IF_EQUAL,
  input  IF_LESS_OR_EQUAL,
  input  [31:0] INTEGER,
  input  [3:0] T1,
  input  [3:0] T2,
  input  [3:0] TS,
  input  IS_ABLE,
  input  CLOCK,
  input  RESET,
  output [3:0] OPCODE_2,
  output [31:0] RT_3,
  output [31:0] RT2,
  output [31:0] RD_2,
  output LI_2,
  output SW_2,
  output LW_2,
  output JUMP_2,
  output IF_EQUAL_2,
  output IF_LESS_OR_EQUAL_2,
  output [31:0] INTEGER_2,
  output [3:0] T1_2,
  output [3:0] T2_2,
  output [3:0] TS_2,
  output IS_ENABLED
);

  wire IF_EQUAL_q, IF_LESS_OR_EQUAL_q, JUMP_q, LI_q, LW_q, not_1_out, SW_q;
  wire [3:0] INTEGER_2_q, INTEGER_3_q, INTEGER_4_q, opcode_q;
  wire [31:0] INTEGER_q, RT_2_q, RT_3_q, RT_q;

  Register #(.width(32), .Select("low")) u_RT (.D(RT), .Q(RT_q), .clk(CLOCK));  // open: en, clr
  Register #(.width(32), .Select("low")) u_RT_2 (.D(RT_2), .Q(RT_2_q), .clk(CLOCK));  // open: en, clr
  Register #(.width(32), .Select("low")) u_RT_3 (.D(RD), .Q(RT_3_q), .clk(CLOCK));  // open: en, clr
  Register #(.width(1), .Select("low")) u_LI (.D(LI), .Q(LI_q), .clk(CLOCK));  // open: en, clr
  Register #(.width(1), .Select("low")) u_SW (.D(SW), .Q(SW_q), .clk(CLOCK));  // open: en, clr
  Register #(.width(4), .Select("low")) u_opcode (.D(OPCODE), .Q(opcode_q), .clk(CLOCK));  // open: en, clr
  Register #(.width(1), .Select("low")) u_LW (.D(LW), .Q(LW_q), .clk(CLOCK));  // open: en, clr
  Register #(.width(1), .Select("low")) u_JUMP (.D(JUMP), .Q(JUMP_q), .clk(CLOCK));  // open: en, clr
  Register #(.width(1), .Select("low")) u_IF_EQUAL (.D(IF_EQUAL), .Q(IF_EQUAL_q), .clk(CLOCK));  // open: en, clr
  Register #(.width(1), .Select("low")) u_IF_LESS_OR_EQUAL (
    .D(IF_LESS_OR_EQUAL), .Q(IF_LESS_OR_EQUAL_q), .clk(CLOCK));  // open: en, clr
  Register #(.width(32), .Select("low")) u_INTEGER (.D(INTEGER), .Q(INTEGER_q), .clk(CLOCK));  // open: en, clr
  Register #(.width(4), .Select("low")) u_INTEGER_2 (.D(T1), .Q(INTEGER_2_q), .clk(CLOCK));  // open: en, clr
  Register #(.width(4), .Select("low")) INTEGER_3 (.D(T2), .Q(INTEGER_3_q), .clk(CLOCK));  // open: en, clr
  Register #(.width(4), .Select("low")) INTEGER_4 (.D(TS), .Q(INTEGER_4_q), .clk(CLOCK));  // open: en, clr
  Register #(.width(1), .Select("low")) u_IF_LESS_OR_EQUAL_2 (
    .D(IS_ABLE), .en(IS_ABLE), .Q(IS_ENABLED), .clk(CLOCK), .clr(RESET));
  Multiplexer #(.width(4)) multiplexer_1 (.in0(opcode_q), .out(OPCODE_2), .sel(not_1_out));  // open: in1, en
  Multiplexer #(.width(32)) multiplexer_2 (.in0(RT_q), .out(RT_3), .sel(not_1_out));  // open: in1, en
  Multiplexer #(.width(32)) multiplexer_3 (.in0(RT_2_q), .out(RT2), .sel(not_1_out));  // open: in1, en
  Multiplexer #(.width(32)) multiplexer_4 (.in0(RT_3_q), .out(RD_2), .sel(not_1_out));  // open: in1, en
  Multiplexer multiplexer_5 (.in0(LI_q), .out(LI_2), .sel(not_1_out));  // open: in1, en
  Multiplexer multiplexer_6 (.in0(SW_q), .out(SW_2), .sel(not_1_out));  // open: in1, en
  Multiplexer multiplexer_7 (.in0(LW_q), .out(LW_2), .sel(not_1_out));  // open: in1, en
  Multiplexer multiplexer_8 (.in0(JUMP_q), .out(JUMP_2), .sel(not_1_out));  // open: in1, en
  Multiplexer multiplexer_9 (.in0(IF_EQUAL_q), .out(IF_EQUAL_2), .sel(not_1_out));  // open: in1, en
  Multiplexer multiplexer_10 (.in0(IF_LESS_OR_EQUAL_q), .out(IF_LESS_OR_EQUAL_2), .sel(not_1_out));  // open: in1, en
  Multiplexer #(.width(32)) multiplexer_11 (.in0(INTEGER_q), .out(INTEGER_2), .sel(not_1_out));  // open: in1, en
  Multiplexer #(.width(4)) multiplexer_12 (.in0(INTEGER_2_q), .out(T1_2), .sel(not_1_out));  // open: in1, en
  Multiplexer #(.width(4)) multiplexer_13 (.in0(INTEGER_3_q), .out(T2_2), .sel(not_1_out));  // open: in1, en
  Multiplexer #(.width(4)) multiplexer_14 (.in0(INTEGER_4_q), .out(TS_2), .sel(not_1_out));  // open: in1, en
  not not_1 (not_1_out, IS_ENABLED);
  // AND_Gate and_1 is placed but not wired
endmodule

module IS_ARITIMETIC (
  input  [3:0] in_1,
  output IS_ARITIMETIC
);

  not not_1 (IS_ARITIMETIC, in_1[3]);
endmodule

module MUX_ULA (
  input  [31:0] RS_ORIGINAL,
  input  [31:0] AFTER_OP,
  input  OPCODE,
  output [31:0] RESULT
);

  Multiplexer #(.width(32)) multiplexer_1 (.in0(RS_ORIGINAL), .in1(AFTER_OP), .out(RESULT), .sel(OPCODE));  // open: en
endmodule

module HANDLE_ERRORS (
  input  HAVE_FUTURE_SIGHT,
  input  [3:0] T1,
  input  [3:0] TS,
  input  [31:0] R1,
  input  [3:0] T2,
  input  [3:0] TS_2,
  input  [31:0] VALUE_FINAL_CODE,
  input  [31:0] RD,
  input  [31:0] R2,
  input  NORMAL_OP,
  input  LI,
  output [31:0] NEW_RT1,
  output [31:0] NEW_RT2,
  output [31:0] NEW_RT3
);

  wire registers_handle_future_1_t1___tsf, registers_handle_future_1_t2___tsf,
       registers_handle_future_1_ts___tsf;

  MUST_SAVE_BEFORE must_save_before_1 (
    .out_6(NEW_RT1), .SAME_REGISTERS(registers_handle_future_1_t1___tsf), .CURRENT(R1),
    .FUTURE_VALUE(VALUE_FINAL_CODE), .in_4(NORMAL_OP), .in_5(LI));
  REGISTERS_HANDLE_FUTURE registers_handle_future_1 (
    .T1(T1), .T2(T2), .TS(TS_2), .TSF(TS), .T1___TSF(registers_handle_future_1_t1___tsf),
    .T2___TSF(registers_handle_future_1_t2___tsf), .TS___TSF(registers_handle_future_1_ts___tsf),
    .HAVE_FUTURE_SIGHT(HAVE_FUTURE_SIGHT));
  MUST_SAVE_BEFORE must_save_before_2 (
    .out_6(NEW_RT2), .SAME_REGISTERS(registers_handle_future_1_t2___tsf), .CURRENT(R2),
    .FUTURE_VALUE(VALUE_FINAL_CODE), .in_4(NORMAL_OP), .in_5(LI));
  MUST_SAVE_BEFORE must_save_before_3 (
    .out_6(NEW_RT3), .SAME_REGISTERS(registers_handle_future_1_ts___tsf), .CURRENT(RD),
    .FUTURE_VALUE(VALUE_FINAL_CODE), .in_4(NORMAL_OP), .in_5(LI));
endmodule

module REGISTERS_HANDLE_FUTURE (
  input  [3:0] T1,
  input  [3:0] T2,
  input  [3:0] TS,
  input  [3:0] TSF,
  input  HAVE_FUTURE_SIGHT,
  output T1___TSF,
  output T2___TSF,
  output TS___TSF
);

  wire comparator_1_eq, comparator_2_eq, comparator_3_eq;

  Comparator #(.width(4)) comparator_1 (.a(T1), .b(TSF), .eq(comparator_1_eq));  // open: gt, lt
  Comparator #(.width(4)) comparator_2 (.a(T2), .b(TSF), .eq(comparator_2_eq));  // open: gt, lt
  Comparator #(.width(4)) comparator_3 (.a(TS), .b(TSF), .eq(comparator_3_eq));  // open: gt, lt
  and and_1 (T1___TSF, comparator_1_eq, HAVE_FUTURE_SIGHT);
  and and_2 (T2___TSF, comparator_2_eq, HAVE_FUTURE_SIGHT);
  and and_3 (TS___TSF, comparator_3_eq, HAVE_FUTURE_SIGHT);
endmodule

module MUST_SAVE_BEFORE (
  input  SAME_REGISTERS,
  input  [31:0] CURRENT,
  input  [31:0] FUTURE_VALUE,
  input  in_4,
  input  in_5,
  output [31:0] out_6
);

  wire and_1_out, or_1_out;

  Multiplexer #(.width(32)) multiplexer_1 (
    .in0(CURRENT), .in1(FUTURE_VALUE), .out(out_6), .sel(and_1_out));  // open: en
  and and_1 (and_1_out, or_1_out, SAME_REGISTERS);
  or or_1 (or_1_out, in_4, in_5);
endmodule

module instruction_position (
  input  [15:0] in_1,
  input  clock,
  input  FLUSH_MEMORY,
  input  RESET,
  input  isStopProcess,
  output [15:0] out_6,
  output NEED_TO_FLUSH
);

  wire not_1_out;

  not not_1 (not_1_out, isStopProcess);
  Register #(.width(16), .Select("low")) register_1 (.D(in_1), .en(not_1_out), .Q(out_6), .clk(clock), .clr(RESET));

  assign NEED_TO_FLUSH = FLUSH_MEMORY;
endmodule

module OUTPUT (
  input  [3:0] OPCODE,
  input  [31:0] RD,
  input  [3:0] TS,
  input  [31:0] ADDRESS,
  output [3:0] OPCODE_2,
  output [31:0] RESULT,
  output [3:0] IN_THIS_REGISTER,
  output [31:0] ADDRESS_2
);


  assign ADDRESS_2 = ADDRESS;
  assign IN_THIS_REGISTER = TS;
  assign OPCODE_2 = OPCODE;
  assign RESULT = RD;
endmodule

module ULA_OUTPUT (
  input  [3:0] OPCODE,
  input  [31:0] R1,
  input  [31:0] R2,
  input  [31:0] RD,
  input  [3:0] T1,
  input  [3:0] T2,
  input  [3:0] TS,
  output [3:0] OPCODE_2,
  output [31:0] R1_2,
  output [31:0] R2_2,
  output [31:0] RD_2,
  output [3:0] T1_2,
  output [3:0] T2_2,
  output [3:0] TS_2
);


  assign OPCODE_2 = OPCODE;
  assign R1_2 = R1;
  assign R2_2 = R2;
  assign RD_2 = RD;
  assign T1_2 = T1;
  assign T2_2 = T2;
  assign TS_2 = TS;
endmodule

module REGISTERS_OUTPUT (
  input  [3:0] OPCODE,
  input  [31:0] R1,
  input  [31:0] R2,
  input  [31:0] RD,
  input  [3:0] T1,
  input  [3:0] T2,
  input  [3:0] TS,
  output [3:0] OPCODE_2,
  output [31:0] R1_2,
  output [31:0] R2_2,
  output [31:0] RD_2,
  output [3:0] T1_2,
  output [3:0] T2_2,
  output [3:0] TS_2
);


  assign OPCODE_2 = OPCODE;
  assign R1_2 = R1;
  assign R2_2 = R2;
  assign RD_2 = RD;
  assign T1_2 = T1;
  assign T2_2 = T2;
  assign TS_2 = TS;
endmodule

module CACHE (
  input  [15:0] posicao,
  input  [31:0] dados,
  input  clock,
  input  toSave,
  input  ValidBit,
  output [31:0] CacheInstruction,
  output isValidCache
);

  wire [3:0] converttag_1_indice, converttag_1_offset;
  wire [7:0] converttag_1_tag;

  convertTag converttag_1 (
    .in_1(posicao), .OFFSET(converttag_1_offset), .INDICE(converttag_1_indice), .TAG(converttag_1_tag));
  validateCache validatecache_1 (
    .TAG(converttag_1_tag), .INDICE(converttag_1_indice), .OFFSET(converttag_1_offset), .Clock(clock),
    .out_8(CacheInstruction), .Is_valid(isValidCache), .Dados(dados), .TO_SAVE(toSave), .isValidBit(ValidBit));
endmodule

module convertTag (
  input  [15:0] in_1,
  output [3:0] OFFSET,
  output [3:0] INDICE,
  output [7:0] TAG
);


  assign INDICE = in_1[7:4];
  assign OFFSET = in_1[3:0];
  assign TAG = in_1[15:8];
endmodule

module validateCache (
  input  [7:0] TAG,
  input  [3:0] INDICE,
  input  [3:0] OFFSET,
  input  [31:0] Dados,
  input  isValidBit,
  input  TO_SAVE,
  input  Clock,
  output [31:0] out_8,
  output Is_valid
);

  wire comparator_1_eq, not_1_out, not_2_out, VALID_BIT_data;
  wire [7:0] TAG_data;
  wire [31:0] DADOS_data;

  not not_1 (not_1_out, TO_SAVE);
  RAM #(.dataWidth(32), .bus("separate"), .Select("high"), .simpleMode("false")) u_DADOS (
    .addr({OFFSET, INDICE}), .din(Dados), .data(DADOS_data), .str(TO_SAVE), .sel(1'b1), .clk(Clock));  // open: ld, clr
  RAM #(.bus("separate"), .Select("high"), .simpleMode("false")) u_TAG (
    .addr({OFFSET, INDICE}), .din(TAG), .data(TAG_data), .str(TO_SAVE), .sel(1'b1), .clk(Clock));  // open: ld, clr
  RAM #(.dataWidth(1), .bus("separate"), .Select("high"), .simpleMode("false")) VALID_BIT (
    .addr({OFFSET, INDICE}), .din(isValidBit), .data(VALID_BIT_data), .str(TO_SAVE), .sel(1'b1), .clk(Clock));  // open: ld, clr
  Comparator comparator_1 (.a(TAG_data), .b(TAG), .eq(comparator_1_eq));  // open: gt, lt
  and and_1 (Is_valid, comparator_1_eq, not_1_out, VALID_BIT_data);
  Multiplexer #(.width(32), .enable("false")) multiplexer_1 (
    .in0(DADOS_data), .out(out_8), .sel(not_2_out));  // open: in1
  not not_2 (not_2_out, Is_valid);
endmodule

module RepetidorAtraso (
  input  clock,
  input  GoodToGo,
  output clockOut
);

  wire d_ff_1_q, d_ff_2_q, d_ff_3_q, d_ff_4_q, not_1_out, or_1_out;

  D_Flip_Flop d_ff_1 (.clk(clock), .D(1'b1), .Q(d_ff_1_q), .reset(or_1_out));  // open: Qn, preset
  D_Flip_Flop d_ff_2 (.clk(clock), .D(d_ff_1_q), .Q(d_ff_2_q), .reset(or_1_out));  // open: Qn, preset
  or or_1 (or_1_out, not_1_out, clockOut);
  not not_1 (not_1_out, GoodToGo);
  D_Flip_Flop d_ff_3 (.clk(clock), .D(d_ff_2_q), .Q(d_ff_3_q), .reset(or_1_out));  // open: Qn, preset
  D_Flip_Flop d_ff_4 (.clk(clock), .D(d_ff_3_q), .Q(d_ff_4_q), .reset(or_1_out));  // open: Qn, preset
  D_Flip_Flop d_ff_5 (.clk(clock), .D(d_ff_4_q), .Q(clockOut));  // open: Qn, preset, reset
endmodule

module atrasoLeve (
  input  clock,
  input  GoodToGo,
  output clockOut
);

  wire d_ff_2_q, not_1_out, or_1_out;

  D_Flip_Flop d_ff_1 (.clk(clock), .D(1'b1), .Q(clockOut), .reset(or_1_out));  // open: Qn, preset
  or or_1 (or_1_out, not_1_out, d_ff_2_q);
  not not_1 (not_1_out, GoodToGo);
  D_Flip_Flop d_ff_2 (.clk(clock), .D(clockOut), .Q(d_ff_2_q), .reset(or_1_out));  // open: Qn, preset
endmodule

module isStopCommand (
  input  [3:0] OPCODE,
  output isStopProcess
);

  Comparator #(.width(4)) comparator_1 (.a(OPCODE), .b(4'b1111), .eq(isStopProcess));  // open: gt, lt
endmodule
